# Fritzing sketch TXos_nano_lcd_rotary (saved by Fritzing 0.9.3b)
circuit board: 9.59351cm x 6.13579cm
breadboards: 1

parts:
  Arduino_Nano_V3 = Arduino Nano (Rev3.0)
  Vin = female pin header, 2 pins [form="♀ (female)"]
  Analog_1 = female pin header, 3 pins [form="♀ (female)"]
  Analog_2 = female pin header, 3 pins [form="♀ (female)"]
  Analog_3 = female pin header, 3 pins [form="♀ (female)"]
  Analog_4 = female pin header, 3 pins [form="♀ (female)"]
  Analog_5 = female pin header, 3 pins [form="♀ (female)"]
  ICSP = shrouded pin header, 6 pins [form="♂ (shrouded male)"]
  R1 = Resistor [tolerance=±5% resistance=10k package=THT]
  R2 = Resistor [tolerance=±5% resistance=22k package=THT]
  Digital_5 = female pin header, 2 pins [form="♀ (female)"]
  Digital_4 = female pin header, 2 pins [form="♀ (female)"]
  Digital_3 = female pin header, 2 pins [form="♀ (female)"]
  Digital_2 = female pin header, 2 pins [form="♀ (female)"]
  Digital_1 = female pin header, 2 pins [form="♀ (female)"]
  PPM = female pin header, 5 pins [form="♀ (female)"]
  Rotary_Encoder = female pin header, 5 pins [form="♀ (female)"]
  TWI1 = female pin header, 4 pins [form="♀ (female)"]
  TWI2 = female pin header, 4 pins [form="♀ (female)"]

nets:
  N1: Arduino_Nano_V3.RESET, ICSP.pin3
  N2: Arduino_Nano_V3.GND, Vin.pin1, Analog_1.pin3, Analog_2.pin3, Analog_3.pin3, Analog_4.pin3, Analog_5.pin3, ICSP.pin4, R1.Pin_1, Digital_5.pin2, Digital_4.pin2, Digital_3.pin2, Digital_2.pin2, Digital_1.pin2, PPM.pin4, Rotary_Encoder.pin1, TWI1.pin4, TWI2.pin4
  N3: Arduino_Nano_V3.D2, Rotary_Encoder.pin5
  N4: Arduino_Nano_V3.D3, Rotary_Encoder.pin4
  N5: Arduino_Nano_V3.D4, Rotary_Encoder.pin3
  N6: Arduino_Nano_V3.D5, PPM.pin1
  N7: Arduino_Nano_V3.D6, Digital_1.pin1
  N8: Arduino_Nano_V3.D7, Digital_2.pin1
  N9: Arduino_Nano_V3.D8, Digital_3.pin1
  N10: Arduino_Nano_V3.D9, Digital_4.pin1
  N11: Arduino_Nano_V3.D10, Digital_5.pin1
  N12: Arduino_Nano_V3.D11/MOSI, ICSP.pin5
  N13: Arduino_Nano_V3.D12/MISO, ICSP.pin1
  N14: Arduino_Nano_V3.VIN, Vin.pin2, PPM.pin3
  N15: Arduino_Nano_V3.5V, Analog_1.pin1, Analog_2.pin1, Analog_3.pin1, Analog_4.pin1, Analog_5.pin1, ICSP.pin6, R2.Pin_0, PPM.pin2, Rotary_Encoder.pin2, TWI1.pin3, TWI2.pin3
  N16: Arduino_Nano_V3.A7, R1.Pin_0, R2.Pin_1
  N17: Arduino_Nano_V3.A6, Analog_5.pin2
  N18: Arduino_Nano_V3.A5, TWI1.pin1, TWI2.pin1
  N19: Arduino_Nano_V3.A4, TWI1.pin2, TWI2.pin2
  N20: Arduino_Nano_V3.A3, Analog_4.pin2
  N21: Arduino_Nano_V3.A2, Analog_3.pin2
  N22: Arduino_Nano_V3.A1, Analog_2.pin2
  N23: Arduino_Nano_V3.A0, Analog_1.pin2
  N24: Arduino_Nano_V3.D13/SCK, ICSP.pin2
