# Fritzing sketch TXos_sim (saved by Fritzing 0.9.3b)
circuit board: 10cm x 8.8cm
breadboards: 1

parts:
  J3 = female pin header, 3 pins [form="♀ (female)"]
  J2 = female pin header, 3 pins [form="♀ (female)"]
  J6 = female pin header, 3 pins [form="♀ (female)"]
  J7 = female pin header, 3 pins [form="♀ (female)"]
  J10 = female pin header, 3 pins [form="♀ (female)"]
  J4 = female pin header, 2 pins [form="♀ (female)"]  # not connected
  J5 = female pin header, 2 pins [form="♀ (female)"]  # not connected
  J9 = female pin header, 2 pins [form="♀ (female)"]  # not connected
  J8 = female pin header, 2 pins [form="♀ (female)"]  # not connected
  J11 = female pin header, 3 pins [form="♀ (female)"]
  J12 = female pin header, 3 pins [form="♀ (female)"]
  J13 = female pin header, 3 pins [form="♀ (female)"]
  J14 = female pin header, 3 pins [form="♀ (female)"]
  J15 = female pin header, 3 pins [form="♀ (female)"]
  J16 = female pin header, 3 pins [form="♀ (female)"]
  J18 = female pin header, 3 pins [form="♀ (female)"]
  J19 = female pin header, 3 pins [form="♀ (female)"]
  J20 = female pin header, 3 pins [form="♀ (female)"]
  J21 = female pin header, 3 pins [form="♀ (female)"]
  J22 = female pin header, 3 pins [form="♀ (female)"]
  J23 = female pin header, 2 pins [form="♀ (female)"]
  J24 = female pin header, 2 pins [form="♀ (female)"]
  J25 = female pin header, 2 pins [form="♀ (female)"]
  J26 = female pin header, 2 pins [form="♀ (female)"]
  J27 = female pin header, 2 pins [form="♀ (female)"]
  J28 = female pin header, 2 pins [form="♀ (female)"]
  J29 = female pin header, 3 pins [form="♀ (female)"]
  J30 = female pin header, 3 pins [form="♀ (female)"]

nets:
  N1: J3.pin1, J12.pin3
  N2: J3.pin2, J12.pin2
  N3: J3.pin3, J12.pin1
  N4: J2.pin1, J13.pin3
  N5: J2.pin2, J13.pin2
  N6: J2.pin3, J13.pin1
  N7: J6.pin1, J15.pin3
  N8: J6.pin2, J15.pin2
  N9: J6.pin3, J15.pin1
  N10: J7.pin1, J14.pin3
  N11: J7.pin2, J14.pin2
  N12: J7.pin3, J14.pin1
  N13: J10.pin2, J24.pin1
  N14: J10.pin3, J24.pin2
  N15: J11.pin1, J30.pin3
  N16: J11.pin2, J30.pin2
  N17: J11.pin3, J30.pin1
  N18: J16.pin1, J29.pin1
  N19: J16.pin2, J29.pin2
  N20: J16.pin3, J29.pin3
  N21: J18.pin2, J27.pin1
  N22: J18.pin3, J27.pin2
  N23: J19.pin2, J26.pin1
  N24: J19.pin3, J26.pin2
  N25: J20.pin2, J23.pin1
  N26: J20.pin3, J23.pin2
  N27: J21.pin2, J28.pin1
  N28: J21.pin3, J28.pin2
  N29: J22.pin2, J25.pin1
  N30: J22.pin3, J25.pin2
